# Fritzing sketch WagonControl (saved by Fritzing 0.9.3b)

parts:
  Part1 = Arduino Nano (Rev3.0) (ICSP)
  Vcc(5V) = Header 11 [package=1x11_smd_no_holes]
  GND = Header 11 [package=1x11_smd_no_holes]
  hc-sr1 = hc-sr04
  BT1 = Bluetooth HC-06u [package=THT]
  Part3 = Black Joystick KY-023
  Motor-R = Header 2 [package=springterminal-2.54mm-2]
  Motor-L = Header 2 [package=springterminal-2.54mm-2]

nets:
  N1: Part1.D2, hc-sr1.Echo
  N2: Part1.D4, BT1.TXD
  N3: Part1.D5, BT1.RXD
  N4: Part1.D7, hc-sr1.Trig
  N5: Part1.D9, Motor-R.2
  N6: Part1.D10, Motor-L.2
  N7: Part1.D11/MOSI, Motor-R.1
  N8: Part1.D12/MISO, Motor-L.1
  N9: Part1.GND, GND.6
  N10: Part1.5V, Vcc(5V).1
  N11: Part1.A1, Part3.VRx
  N12: Part1.A0, Part3.VRy
  N13: Vcc(5V).2, Part3.+5V
  N14: Vcc(5V).5, BT1.VCC
  N15: Vcc(5V).11, hc-sr1.VCC
  N16: GND.1, Part3.GND
  N17: GND.8, BT1.GND
  N18: GND.11, hc-sr1.GND

custom parts:
  Bluetooth HC-06u: Bluetooth HC-06 - face up, pins down 16.5mm x 37.5mm PCB
  Black Joystick KY-023: Description: The joystick is a combination of 2 analoog potentiometer and a digital switch. Arduino GND --> Module pin - Arduino +5V --> Module pin +5V Arduino Analoog 0 --> Module VRx Arduino Analoog 1 --> Module VRy Arduino Digital --> Module SW Dimensions: 1" x 1.25"
